// Logisim project my copy.circ as structural Verilog
module and_IC (
  input  in_1,
  input  in_2,
  input  in_3,
  input  in_4,
  input  in_5,
  input  in_6,
  input  in_7,
  input  in_8,
  output out_9,
  output out_10,
  output out_11,
  output out_12
);

  and and_1 (out_9, in_1, in_2);
  and and_2 (out_10, in_3, in_4);
  and and_3 (out_11, in_5, in_6);
  and and_4 (out_12, in_7, in_8);
endmodule

module or_IC (
  input  in_1,
  input  in_2,
  input  in_3,
  input  in_4,
  input  in_5,
  input  in_6,
  input  in_7,
  input  in_8,
  output out_9,
  output out_10,
  output out_11,
  output out_12
);

  or or_1 (out_9, in_1, in_2);
  or or_2 (out_10, in_3, in_4);
  or or_3 (out_11, in_5, in_6);
  or or_4 (out_12, in_7, in_8);
endmodule

module not_IC (
  input  in_1,
  input  in_2,
  input  in_3,
  input  in_4,
  input  in_5,
  input  in_6,
  output out_7,
  output out_8,
  output out_9,
  output out_10,
  output out_11,
  output out_12
);

  not not_1 (out_7, in_1);
  not not_2 (out_8, in_2);
  not not_3 (out_9, in_3);
  not not_4 (out_10, in_4);
  not not_5 (out_11, in_5);
  not not_6 (out_12, in_6);
endmodule

module nor_IC (
  input  in_1,
  input  in_2,
  input  in_3,
  input  in_4,
  input  in_5,
  input  in_6,
  input  in_7,
  input  in_8,
  output out_9,
  output out_10,
  output out_11,
  output out_12
);

  nor nor_1 (out_9, in_1, in_2);
  nor nor_2 (out_10, in_3, in_4);
  nor nor_3 (out_11, in_5, in_6);
  nor nor_4 (out_12, in_7, in_8);
endmodule

module xor_IC (
  input  in_1,
  input  in_2,
  input  in_3,
  input  in_4,
  input  in_5,
  input  in_6,
  input  in_7,
  input  in_8,
  output out_9,
  output out_10,
  output out_11,
  output out_12
);

  xor xor_1 (out_9, in_1, in_2);
  xor xor_2 (out_10, in_3, in_4);
  xor xor_3 (out_11, in_5, in_6);
  xor xor_4 (out_12, in_7, in_8);
endmodule

module _4_1_Mux (
  input  S2,
  input  S1,
  input  A,
  input  B,
  input  C,
  input  D,
  output out_7
);

  wire and_1_out, and_2_out, and_3_out, and_4_out, not_1_out, not_2_out;

  not not_1 (not_1_out, S2);
  not not_2 (not_2_out, S1);
  and and_1 (and_1_out, A, not_2_out, not_1_out);
  and and_2 (and_2_out, B, not_2_out, S2);
  and and_3 (and_3_out, C, S1, not_1_out);
  and and_4 (and_4_out, D, S1, S2);
  or or_1 (out_7, and_1_out, and_2_out, and_3_out, and_4_out);
endmodule

module lab_1_task (
  input  A1,
  input  B1,
  input  A2,
  input  B2,
  input  LSB,
  input  MSB,
  output F1,
  output F2
);

  wire and_ic_1_out_9, and_ic_1_out_10, not_ic_1_out_7, not_ic_1_out_8, or_ic_1_out_9, or_ic_1_out_10,
       xor_ic_1_out_9, xor_ic_1_out_10;

  and_IC and_ic_1 (
    .in_1(A1), .in_2(B1), .in_3(A2), .in_4(B2), .out_9(and_ic_1_out_9), .out_10(and_ic_1_out_10));  // open: in_5, in_6, in_7, in_8, out_11, out_12
  or_IC or_ic_1 (
    .in_1(A1), .in_2(B1), .in_3(A2), .in_4(B2), .out_9(or_ic_1_out_9), .out_10(or_ic_1_out_10));  // open: in_5, in_6, in_7, in_8, out_11, out_12
  xor_IC xor_ic_1 (
    .in_1(A1), .in_2(B1), .in_3(A2), .in_4(B2), .out_9(xor_ic_1_out_9), .out_10(xor_ic_1_out_10));  // open: in_5, in_6, in_7, in_8, out_11, out_12
  not_IC not_ic_1 (
    .in_1(A1), .in_2(A2), .out_7(not_ic_1_out_7), .out_8(not_ic_1_out_8));  // open: in_3, in_4, in_5, in_6, out_9, out_10, out_11, out_12
  _4_1_Mux u_4_1_mux_1 (
    .S2(LSB), .S1(MSB), .A(and_ic_1_out_9), .B(or_ic_1_out_9), .out_7(F1), .C(xor_ic_1_out_9),
    .D(not_ic_1_out_7));
  _4_1_Mux u_4_1_mux_2 (
    .S2(LSB), .S1(MSB), .A(and_ic_1_out_10), .B(or_ic_1_out_10), .out_7(F2), .C(xor_ic_1_out_10),
    .D(not_ic_1_out_8));

  // Notes on the sheet:
  //   Istiak Ahmed Sheam
  //   ID: 1911139642
  //   2 Bit Logic Unit
endmodule

module _4_Bit_Adder_IC (
  input  A,
  input  B,
  input  cin,
  input  A_2,
  input  B_2,
  input  A_3,
  input  B_3,
  input  A_4,
  input  B_4,
  output sum,
  output sum_2,
  output sum_3,
  output sum_4,
  output cout
);

  wire and_1_out, and_2_out, and_3_out, and_4_out, and_5_out, and_6_out, and_7_out, and_8_out, or_1_out,
       or_2_out, or_3_out, xor_1_out, xor_2_out, xor_3_out, xor_4_out;

  xor xor_1 (xor_1_out, A, B);
  and and_1 (and_1_out, A, B);
  xor xor_2 (xor_2_out, A_2, B_2);
  and and_2 (and_2_out, A_2, B_2);
  xor xor_3 (xor_3_out, A_3, B_3);
  and and_3 (and_3_out, A_3, B_3);
  xor xor_4 (xor_4_out, A_4, B_4);
  and and_4 (and_4_out, A_4, B_4);
  and and_5 (and_5_out, xor_1_out, cin);
  and and_6 (and_6_out, xor_2_out, or_1_out);
  and and_7 (and_7_out, xor_3_out, or_2_out);
  and and_8 (and_8_out, xor_4_out, or_3_out);
  xor xor_5 (sum, xor_1_out, cin);
  or or_1 (or_1_out, and_5_out, and_1_out);
  xor xor_6 (sum_2, xor_2_out, or_1_out);
  or or_2 (or_2_out, and_6_out, and_2_out);
  xor xor_7 (sum_3, xor_3_out, or_2_out);
  or or_3 (or_3_out, and_7_out, and_3_out);
  xor xor_8 (sum_4, xor_4_out, or_3_out);
  or or_4 (cout, and_8_out, and_4_out);
endmodule

module D_Flip_Flop_IC (
  input  in_1,
  input  in_2,
  input  in_3,
  input  in_4,
  output out_5,
  output out_6
);

  wire nand_1_out, nand_2_out, nand_3_out, nand_4_out, not_1_out, not_2_out;

  not not_1 (not_1_out, in_1);
  not not_2 (not_2_out, in_4);
  nand nand_1 (nand_1_out, not_1_out, nand_4_out, nand_2_out);
  nand nand_2 (nand_2_out, nand_1_out, in_2, not_2_out);
  nand nand_3 (nand_3_out, nand_2_out, in_2, nand_4_out);
  nand nand_4 (nand_4_out, nand_3_out, in_3, not_2_out);
  nand nand_5 (out_5, not_1_out, nand_2_out, out_6);
  nand nand_6 (out_6, out_5, nand_3_out, not_2_out);
endmodule

module lab_2_task (
  input  A0,
  input  A1,
  input  Cin,
  input  A2,
  input  A3,
  input  B0,
  input  B1,
  input  B2,
  input  B3,
  input  in_10,
  input  S0,
  input  S1,
  output out_13,
  output S2,
  output out_15,
  output S0_2,
  output carry
);

  wire n4_1_mux_1_out_7, n4_1_mux_2_out_7, n4_1_mux_3_out_7, n4_1_mux_4_out_7, not_ic_1_out_7,
       not_ic_1_out_8, not_ic_1_out_9, not_ic_1_out_11, not_ic_1_out_12;

  not_IC not_ic_1 (
    .in_1(B0), .in_2(B1), .in_3(B2), .in_5(B3), .in_6(in_10), .out_7(not_ic_1_out_7), .out_8(not_ic_1_out_8),
    .out_9(not_ic_1_out_9), .out_11(not_ic_1_out_11), .out_12(not_ic_1_out_12));  // open: in_4, out_10
  _4_1_Mux u_4_1_mux_1 (
    .S2(S0), .S1(S1), .A(B0), .B(not_ic_1_out_7), .out_7(n4_1_mux_1_out_7), .C(in_10), .D(not_ic_1_out_12));
  _4_1_Mux u_4_1_mux_2 (
    .S2(S0), .S1(S1), .A(B1), .B(not_ic_1_out_8), .out_7(n4_1_mux_2_out_7), .C(in_10), .D(not_ic_1_out_12));
  _4_1_Mux u_4_1_mux_3 (
    .S2(S0), .S1(S1), .A(B2), .B(not_ic_1_out_9), .out_7(n4_1_mux_3_out_7), .C(in_10), .D(not_ic_1_out_12));
  _4_1_Mux u_4_1_mux_4 (
    .S2(S0), .S1(S1), .A(B3), .B(not_ic_1_out_11), .out_7(n4_1_mux_4_out_7), .C(in_10), .D(not_ic_1_out_12));
  _4_Bit_Adder_IC u_4_bit_adder_ic_1 (
    .A(A0), .B(n4_1_mux_1_out_7), .cin(Cin), .A_2(A1), .B_2(n4_1_mux_2_out_7), .A_3(A2),
    .B_3(n4_1_mux_3_out_7), .A_4(A3), .B_4(n4_1_mux_4_out_7), .sum(S0_2), .sum_2(out_15), .sum_3(S2),
    .sum_4(out_13), .cout(carry));

  // Notes on the sheet:
  //   S3
  //   S1
endmodule

module lab_3_task (
  input  A4,
  input  A3,
  input  A2,
  input  A1,
  input  B4,
  input  B3,
  input  B2,
  input  B1,
  output S8,
  output S7,
  output S6,
  output S5,
  output S4,
  output S3,
  output S2,
  output S1
);

  wire and_ic_1_out_9, and_ic_1_out_10, and_ic_1_out_11, and_ic_1_out_12, and_ic_2_out_9, and_ic_2_out_10,
       and_ic_2_out_11, and_ic_2_out_12, and_ic_3_out_9, and_ic_3_out_10, and_ic_3_out_11, and_ic_3_out_12,
       and_ic_4_out_10, and_ic_4_out_11, and_ic_4_out_12, n4_bit_adder_ic_1_cout, n4_bit_adder_ic_1_sum_2,
       n4_bit_adder_ic_1_sum_3, n4_bit_adder_ic_1_sum_4, n4_bit_adder_ic_2_cout, n4_bit_adder_ic_2_sum_2,
       n4_bit_adder_ic_2_sum_3, n4_bit_adder_ic_2_sum_4;

  and_IC and_ic_1 (
    .in_1(A4), .in_2(B1), .in_3(A4), .in_4(B2), .in_5(A4), .in_6(B4), .in_7(A4), .in_8(B3),
    .out_9(and_ic_1_out_9), .out_10(and_ic_1_out_10), .out_11(and_ic_1_out_11), .out_12(and_ic_1_out_12));
  and_IC and_ic_2 (
    .in_1(A3), .in_2(B1), .in_3(A3), .in_4(B2), .in_5(A3), .in_6(B4), .in_7(A3), .in_8(B3),
    .out_9(and_ic_2_out_9), .out_10(and_ic_2_out_10), .out_11(and_ic_2_out_11), .out_12(and_ic_2_out_12));
  and_IC and_ic_3 (
    .in_1(A2), .in_2(B1), .in_3(A2), .in_4(B2), .in_5(A2), .in_6(B4), .in_7(A2), .in_8(B3),
    .out_9(and_ic_3_out_9), .out_10(and_ic_3_out_10), .out_11(and_ic_3_out_11), .out_12(and_ic_3_out_12));
  and_IC and_ic_4 (
    .in_1(A1), .in_2(B1), .in_3(A1), .in_4(B2), .in_5(A1), .in_6(B4), .in_7(A1), .in_8(B3), .out_9(S1),
    .out_10(and_ic_4_out_10), .out_11(and_ic_4_out_11), .out_12(and_ic_4_out_12));
  _4_Bit_Adder_IC u_4_bit_adder_ic_1 (
    .A(and_ic_4_out_10), .B(and_ic_3_out_9), .cin(1'b0), .A_2(and_ic_4_out_12), .B_2(and_ic_3_out_10),
    .A_3(and_ic_4_out_11), .B_3(and_ic_3_out_12), .A_4(1'b0), .B_4(and_ic_3_out_11), .sum(S2),
    .sum_2(n4_bit_adder_ic_1_sum_2), .sum_3(n4_bit_adder_ic_1_sum_3), .sum_4(n4_bit_adder_ic_1_sum_4),
    .cout(n4_bit_adder_ic_1_cout));
  _4_Bit_Adder_IC u_4_bit_adder_ic_2 (
    .A(n4_bit_adder_ic_1_sum_2), .B(and_ic_2_out_9), .cin(1'b0), .A_2(n4_bit_adder_ic_1_sum_3),
    .B_2(and_ic_2_out_10), .A_3(n4_bit_adder_ic_1_sum_4), .B_3(and_ic_2_out_12),
    .A_4(n4_bit_adder_ic_1_cout), .B_4(and_ic_2_out_11), .sum(S3), .sum_2(n4_bit_adder_ic_2_sum_2),
    .sum_3(n4_bit_adder_ic_2_sum_3), .sum_4(n4_bit_adder_ic_2_sum_4), .cout(n4_bit_adder_ic_2_cout));
  _4_Bit_Adder_IC u_4_bit_adder_ic_3 (
    .A(n4_bit_adder_ic_2_sum_2), .B(and_ic_1_out_9), .cin(1'b0), .A_2(n4_bit_adder_ic_2_sum_3),
    .B_2(and_ic_1_out_10), .A_3(n4_bit_adder_ic_2_sum_4), .B_3(and_ic_1_out_12),
    .A_4(n4_bit_adder_ic_2_cout), .B_4(and_ic_1_out_11), .sum(S4), .sum_2(S5), .sum_3(S6), .sum_4(S7),
    .cout(S8));
endmodule

module lab_4_task (
  input  Up,
  input  Down,
  input  in_3,
  input  Reset,
  input  [3:0] Set,
  output A,
  output B,
  output C,
  output D
);

  wire and_ic_1_out_9, and_ic_1_out_10, and_ic_1_out_11, and_ic_1_out_12, and_ic_2_out_9, and_ic_2_out_11,
       and_ic_2_out_12, d_flip_flop_ic_1_out_6, d_flip_flop_ic_2_out_6, d_flip_flop_ic_3_out_6,
       not_ic_1_out_7, or_ic_1_out_9, or_ic_1_out_10, or_ic_1_out_11, or_ic_1_out_12, xor_ic_1_out_9,
       xor_ic_1_out_10, xor_ic_1_out_11, xor_ic_1_out_12;

  not_IC not_ic_1 (
    .in_1(Up), .out_7(not_ic_1_out_7));  // open: in_2, in_3, in_4, in_5, in_6, out_8, out_9, out_10, out_11, out_12
  and_IC and_ic_1 (
    .in_1(not_ic_1_out_7), .in_2(Down), .in_3(and_ic_1_out_9), .in_4(d_flip_flop_ic_1_out_6),
    .in_5(and_ic_1_out_10), .in_6(d_flip_flop_ic_2_out_6), .in_7(Up), .in_8(D), .out_9(and_ic_1_out_9),
    .out_10(and_ic_1_out_10), .out_11(and_ic_1_out_11), .out_12(and_ic_1_out_12));
  and_IC and_ic_2 (
    .in_1(and_ic_1_out_11), .in_2(d_flip_flop_ic_3_out_6), .in_5(and_ic_2_out_12), .in_6(B),
    .in_7(and_ic_1_out_12), .in_8(C), .out_9(and_ic_2_out_9), .out_11(and_ic_2_out_11),
    .out_12(and_ic_2_out_12));  // open: in_3, in_4, out_10
  or_IC or_ic_1 (
    .in_1(Up), .in_2(and_ic_1_out_9), .in_3(and_ic_1_out_10), .in_4(and_ic_1_out_12), .in_5(and_ic_2_out_9),
    .in_6(and_ic_2_out_11), .in_7(and_ic_1_out_11), .in_8(and_ic_2_out_12), .out_9(or_ic_1_out_9),
    .out_10(or_ic_1_out_10), .out_11(or_ic_1_out_11), .out_12(or_ic_1_out_12));
  xor_IC xor_ic_1 (
    .in_1(or_ic_1_out_9), .in_2(D), .in_3(or_ic_1_out_10), .in_4(C), .in_5(or_ic_1_out_11), .in_6(A),
    .in_7(or_ic_1_out_12), .in_8(B), .out_9(xor_ic_1_out_9), .out_10(xor_ic_1_out_10),
    .out_11(xor_ic_1_out_11), .out_12(xor_ic_1_out_12));
  D_Flip_Flop_IC d_flip_flop_ic_1 (
    .in_1(Set[0]), .in_3(xor_ic_1_out_9), .in_4(Reset), .out_5(D), .out_6(d_flip_flop_ic_1_out_6), .in_2(in_3));
  D_Flip_Flop_IC d_flip_flop_ic_2 (
    .in_1(Set[1]), .in_3(xor_ic_1_out_10), .in_4(Reset), .out_5(C), .out_6(d_flip_flop_ic_2_out_6),
    .in_2(in_3));
  D_Flip_Flop_IC d_flip_flop_ic_3 (
    .in_1(Set[2]), .in_3(xor_ic_1_out_12), .in_4(Reset), .out_5(B), .out_6(d_flip_flop_ic_3_out_6),
    .in_2(in_3));
  D_Flip_Flop_IC d_flip_flop_ic_4 (
    .in_1(Set[3]), .in_3(xor_ic_1_out_11), .in_4(Reset), .out_5(A), .in_2(in_3));  // open: out_6
endmodule

module Register_File (
  input  [15:0] in_1,
  input  [3:0] RD,
  input  [3:0] RS,
  input  [3:0] RT,
  input  Enable_Writing,
  input  in_6,
  output [15:0] out_7,
  output [15:0] out_8
);

  wire and_1_out, and_2_out, and_3_out, and_4_out, and_5_out, and_6_out, and_7_out, and_8_out, and_9_out,
       and_10_out, and_11_out, and_12_out, and_13_out, and_14_out, and_15_out, and_16_out, decoder_1_out0,
       decoder_1_out1, decoder_1_out2, decoder_1_out3, decoder_1_out4, decoder_1_out5, decoder_1_out6,
       decoder_1_out7, decoder_1_out8, decoder_1_out9, decoder_1_out10, decoder_1_out11, decoder_1_out12,
       decoder_1_out13, decoder_1_out14, decoder_1_out15;
  wire [15:0] register_1_q, register_2_q, register_3_q, register_4_q, register_5_q, register_6_q,
       register_7_q, register_8_q, register_9_q, register_10_q, register_11_q, register_12_q, register_13_q,
       register_14_q, register_15_q, register_16_q;

  Decoder #(.select(4), .enable("false")) decoder_1 (
    .out0(decoder_1_out0), .out1(decoder_1_out1), .out2(decoder_1_out2), .out3(decoder_1_out3),
    .out4(decoder_1_out4), .out5(decoder_1_out5), .out6(decoder_1_out6), .out7(decoder_1_out7),
    .out8(decoder_1_out8), .out9(decoder_1_out9), .out10(decoder_1_out10), .out11(decoder_1_out11),
    .out12(decoder_1_out12), .out13(decoder_1_out13), .out14(decoder_1_out14), .out15(decoder_1_out15),
    .sel(RD));
  and and_1 (and_1_out, decoder_1_out0, Enable_Writing);
  and and_2 (and_2_out, decoder_1_out1, Enable_Writing);
  and and_3 (and_3_out, decoder_1_out2, Enable_Writing);
  and and_4 (and_4_out, decoder_1_out3, Enable_Writing);
  and and_5 (and_5_out, decoder_1_out4, Enable_Writing);
  and and_6 (and_6_out, decoder_1_out5, Enable_Writing);
  and and_7 (and_7_out, decoder_1_out6, Enable_Writing);
  and and_8 (and_8_out, decoder_1_out7, Enable_Writing);
  and and_9 (and_9_out, decoder_1_out8, Enable_Writing);
  and and_10 (and_10_out, decoder_1_out9, Enable_Writing);
  and and_11 (and_11_out, decoder_1_out10, Enable_Writing);
  and and_12 (and_12_out, decoder_1_out11, Enable_Writing);
  and and_13 (and_13_out, decoder_1_out12, Enable_Writing);
  and and_14 (and_14_out, decoder_1_out13, Enable_Writing);
  and and_15 (and_15_out, decoder_1_out14, Enable_Writing);
  and and_16 (and_16_out, decoder_1_out15, Enable_Writing);
  Register #(.width(16)) register_1 (.D(in_1), .en(and_1_out), .Q(register_1_q), .clk(in_6));  // open: clr
  Register #(.width(16)) register_2 (.D(in_1), .en(and_2_out), .Q(register_2_q), .clk(in_6));  // open: clr
  Register #(.width(16)) register_3 (.D(in_1), .en(and_3_out), .Q(register_3_q), .clk(in_6));  // open: clr
  Register #(.width(16)) register_4 (.D(in_1), .en(and_4_out), .Q(register_4_q), .clk(in_6));  // open: clr
  Register #(.width(16)) register_5 (.D(in_1), .en(and_5_out), .Q(register_5_q), .clk(in_6));  // open: clr
  Register #(.width(16)) register_6 (.D(in_1), .en(and_6_out), .Q(register_6_q), .clk(in_6));  // open: clr
  Register #(.width(16)) register_7 (.D(in_1), .en(and_7_out), .Q(register_7_q), .clk(in_6));  // open: clr
  Register #(.width(16)) register_8 (.D(in_1), .en(and_8_out), .Q(register_8_q), .clk(in_6));  // open: clr
  Register #(.width(16)) register_9 (.D(in_1), .en(and_9_out), .Q(register_9_q), .clk(in_6));  // open: clr
  Register #(.width(16)) register_10 (.D(in_1), .en(and_10_out), .Q(register_10_q), .clk(in_6));  // open: clr
  Register #(.width(16)) register_11 (.D(in_1), .en(and_11_out), .Q(register_11_q), .clk(in_6));  // open: clr
  Register #(.width(16)) register_12 (.D(in_1), .en(and_12_out), .Q(register_12_q), .clk(in_6));  // open: clr
  Register #(.width(16)) register_13 (.D(in_1), .en(and_13_out), .Q(register_13_q), .clk(in_6));  // open: clr
  Register #(.width(16)) register_14 (.D(in_1), .en(and_14_out), .Q(register_14_q), .clk(in_6));  // open: clr
  Register #(.width(16)) register_15 (.D(in_1), .en(and_15_out), .Q(register_15_q), .clk(in_6));  // open: clr
  Register #(.width(16)) register_16 (.D(in_1), .en(and_16_out), .Q(register_16_q), .clk(in_6));  // open: clr
  Multiplexer #(.select(4), .width(16), .enable("false")) multiplexer_1 (
    .in0(register_1_q), .in1(register_2_q), .in2(register_3_q), .in3(register_4_q), .in4(register_5_q),
    .in5(register_6_q), .in6(register_7_q), .in7(register_8_q), .in8(register_9_q), .in9(register_10_q),
    .in10(register_11_q), .in11(register_12_q), .in12(register_13_q), .in13(register_14_q),
    .in14(register_15_q), .in15(register_16_q), .out(out_7), .sel(RS));
  Multiplexer #(.select(4), .width(16), .enable("false")) multiplexer_2 (
    .in0(register_1_q), .in1(register_2_q), .in2(register_3_q), .in3(register_4_q), .in4(register_5_q),
    .in5(register_6_q), .in6(register_7_q), .in7(register_8_q), .in8(register_9_q), .in9(register_10_q),
    .in10(register_11_q), .in11(register_12_q), .in12(register_13_q), .in13(register_14_q),
    .in14(register_15_q), .in15(register_16_q), .out(out_8), .sel(RT));

  // Notes on the sheet:
  //   Write Data
  //   clock
  //   R0
  //   R1
  //   R2
  //   R3
  //   R4
  //   R5
  //   R6
  //   R7
  //   R8
  //   R9
  //   R10
  //   R11
  //   R12
  //   R13
  //   R14
  //   R15
  //   Data 1
  //   Data 2
endmodule

module Instruction_fetch (
  input  [15:0] in_1,
  input  in_2,
  output [3:0] op_code,
  output [3:0] RS,
  output [3:0] RT,
  output [3:0] RD_Imm,
  output [15:0] out_7,
  output [15:0] out_8
);

  wire clock_1_out;
  wire [15:0] adder_1_out, register_1_q;

  Clock clock_1 (.out(clock_1_out));
  Register #(.width(16)) register_1 (.D(adder_1_out), .Q(register_1_q), .clk(clock_1_out));  // open: en, clr
  Adder #(.width(16)) adder_1 (.a(register_1_q), .b(16'h1), .out(adder_1_out));  // open: cin, cout
  ROM #(.addrWidth(16), .dataWidth(16)) rom_1 (.addr(register_1_q), .data({op_code, RS, RT, RD_Imm}));  // open: sel
  Register_File register_file_1 (
    .in_1(in_1), .RD(RD_Imm), .RS(RS), .RT(RT), .Enable_Writing(in_2), .in_6(clock_1_out), .out_7(out_7),
    .out_8(out_8));

  // Notes on the sheet:
  //   writing data
  //   writhing enable
  //   clock
  //   PC
  //   contents of rom_1 (hex, n*v repeats v):
  //   123 330 5*0 101 0 0 0 1111 0 0 0 101
  //   Data 1
  //   Data 2
endmodule

module _1_bit_ALU (
  input  B,
  input  Cin,
  input  A,
  input  B_inv,
  input  A_inv,
  input  [1:0] alu_op,
  output out_7,
  output out_8
);

  wire adder_1_out, and_1_out, multiplexer_1_out, multiplexer_2_out, not_1_out, not_2_out, or_1_out,
       xor_1_out;

  Multiplexer #(.enable("false")) multiplexer_1 (.in0(B), .in1(not_1_out), .out(multiplexer_1_out), .sel(B_inv));
  not not_1 (not_1_out, B);
  not not_2 (not_2_out, A);
  Multiplexer #(.enable("false")) multiplexer_2 (.in0(A), .in1(not_2_out), .out(multiplexer_2_out), .sel(A_inv));
  and and_1 (and_1_out, multiplexer_2_out, multiplexer_1_out);
  or or_1 (or_1_out, multiplexer_2_out, multiplexer_1_out);
  Adder #(.width(1)) adder_1 (.a(multiplexer_2_out), .b(multiplexer_1_out), .out(adder_1_out), .cin(Cin), .cout(out_8));
  xor xor_1 (xor_1_out, multiplexer_2_out, multiplexer_1_out);
  Multiplexer #(.select(2), .enable("false")) multiplexer_3 (
    .in0(and_1_out), .in1(or_1_out), .in2(adder_1_out), .in3(xor_1_out), .out(out_7), .sel(alu_op));
endmodule

module _16_bit_ALU (
  input  in_1,
  input  in_2,
  input  in_3,
  input  [15:0] A,
  input  [15:0] B,
  input  [1:0] ALU_op,
  output [15:0] out_7,
  output Zero,
  output overflow
);

  wire n1_bit_alu_1_out_8, n1_bit_alu_2_out_8, n1_bit_alu_3_out_8, n1_bit_alu_4_out_8, n1_bit_alu_5_out_8,
       n1_bit_alu_6_out_8, n1_bit_alu_7_out_8, n1_bit_alu_8_out_8, n1_bit_alu_9_out_8, n1_bit_alu_10_out_8,
       n1_bit_alu_11_out_8, n1_bit_alu_12_out_8, n1_bit_alu_13_out_8, n1_bit_alu_14_out_8,
       n1_bit_alu_15_out_8, n1_bit_alu_16_out_8;

  _1_bit_ALU u_1_bit_alu_1 (
    .B_inv(in_3), .A_inv(in_1), .alu_op(ALU_op), .out_7(out_7[0]), .out_8(n1_bit_alu_1_out_8), .B(B[0]),
    .A(A[0]), .Cin(in_2));
  _1_bit_ALU u_1_bit_alu_2 (
    .B_inv(in_3), .A_inv(in_1), .alu_op(ALU_op), .out_7(out_7[1]), .out_8(n1_bit_alu_2_out_8), .B(B[1]),
    .A(A[1]), .Cin(n1_bit_alu_1_out_8));
  _1_bit_ALU u_1_bit_alu_3 (
    .B_inv(in_3), .A_inv(in_1), .alu_op(ALU_op), .out_7(out_7[2]), .out_8(n1_bit_alu_3_out_8), .B(B[2]),
    .A(A[2]), .Cin(n1_bit_alu_2_out_8));
  _1_bit_ALU u_1_bit_alu_4 (
    .B_inv(in_3), .A_inv(in_1), .alu_op(ALU_op), .out_7(out_7[3]), .out_8(n1_bit_alu_4_out_8), .B(B[3]),
    .A(A[3]), .Cin(n1_bit_alu_3_out_8));
  _1_bit_ALU u_1_bit_alu_5 (
    .B_inv(in_3), .A_inv(in_1), .alu_op(ALU_op), .out_7(out_7[4]), .out_8(n1_bit_alu_5_out_8), .B(B[4]),
    .A(A[4]), .Cin(n1_bit_alu_4_out_8));
  _1_bit_ALU u_1_bit_alu_6 (
    .B_inv(in_3), .A_inv(in_1), .alu_op(ALU_op), .out_7(out_7[5]), .out_8(n1_bit_alu_6_out_8), .B(B[5]),
    .A(A[5]), .Cin(n1_bit_alu_5_out_8));
  _1_bit_ALU u_1_bit_alu_7 (
    .B_inv(in_3), .A_inv(in_1), .alu_op(ALU_op), .out_7(out_7[6]), .out_8(n1_bit_alu_7_out_8), .B(B[6]),
    .A(A[6]), .Cin(n1_bit_alu_6_out_8));
  _1_bit_ALU u_1_bit_alu_8 (
    .B_inv(in_3), .A_inv(in_1), .alu_op(ALU_op), .out_7(out_7[7]), .out_8(n1_bit_alu_8_out_8), .B(B[7]),
    .A(A[7]), .Cin(n1_bit_alu_7_out_8));
  _1_bit_ALU u_1_bit_alu_9 (
    .B_inv(in_3), .A_inv(in_1), .alu_op(ALU_op), .out_7(out_7[8]), .out_8(n1_bit_alu_9_out_8), .B(B[8]),
    .A(A[8]), .Cin(n1_bit_alu_8_out_8));
  _1_bit_ALU u_1_bit_alu_10 (
    .B_inv(in_3), .A_inv(in_1), .alu_op(ALU_op), .out_7(out_7[9]), .out_8(n1_bit_alu_10_out_8), .B(B[9]),
    .A(A[9]), .Cin(n1_bit_alu_9_out_8));
  _1_bit_ALU u_1_bit_alu_11 (
    .B_inv(in_3), .A_inv(in_1), .alu_op(ALU_op), .out_7(out_7[10]), .out_8(n1_bit_alu_11_out_8), .B(B[10]),
    .A(A[10]), .Cin(n1_bit_alu_10_out_8));
  _1_bit_ALU u_1_bit_alu_12 (
    .B_inv(in_3), .A_inv(in_1), .alu_op(ALU_op), .out_7(out_7[11]), .out_8(n1_bit_alu_12_out_8), .B(B[11]),
    .A(A[11]), .Cin(n1_bit_alu_11_out_8));
  _1_bit_ALU u_1_bit_alu_13 (
    .B_inv(in_3), .A_inv(in_1), .alu_op(ALU_op), .out_7(out_7[12]), .out_8(n1_bit_alu_13_out_8), .B(B[12]),
    .A(A[12]), .Cin(n1_bit_alu_12_out_8));
  _1_bit_ALU u_1_bit_alu_14 (
    .B_inv(in_3), .A_inv(in_1), .alu_op(ALU_op), .out_7(out_7[13]), .out_8(n1_bit_alu_14_out_8), .B(B[13]),
    .A(A[13]), .Cin(n1_bit_alu_13_out_8));
  _1_bit_ALU u_1_bit_alu_15 (
    .B_inv(in_3), .A_inv(in_1), .alu_op(ALU_op), .out_7(out_7[14]), .out_8(n1_bit_alu_15_out_8), .B(B[14]),
    .A(A[14]), .Cin(n1_bit_alu_14_out_8));
  _1_bit_ALU u_1_bit_alu_16 (
    .B_inv(in_3), .A_inv(in_1), .alu_op(ALU_op), .out_7(out_7[15]), .out_8(n1_bit_alu_16_out_8), .B(B[15]),
    .A(A[15]), .Cin(n1_bit_alu_15_out_8));
  xor xor_1 (overflow, n1_bit_alu_15_out_8, n1_bit_alu_16_out_8);
  nor nor_1 (Zero, out_7[0], out_7[1], out_7[2], out_7[3], out_7[4], out_7[5], out_7[6], out_7[7], out_7[9], out_7[10], out_7[11], out_7[12], out_7[13], out_7[14], out_7[15], out_7[8]);
endmodule

module R__type_data_path (
  input  in_1,
  input  in_2,
  input  in_3,
  input  [1:0] in_4,
  input  [15:0] in_5,
  input  in_6,
  output [3:0] op_code,
  output [3:0] RS,
  output [15:0] out_9,
  output [3:0] RT,
  output [3:0] RD_Imm,
  output zero,
  output [15:0] Result,
  output over_flow,
  output [15:0] out_15
);

  wire clock_1_out;
  wire [15:0] adder_1_out, register_1_q;

  Clock clock_1 (.out(clock_1_out));
  Register #(.width(16)) register_1 (.D(adder_1_out), .Q(register_1_q), .clk(clock_1_out));  // open: en, clr
  Adder #(.width(16)) adder_1 (.a(register_1_q), .b(16'h1), .out(adder_1_out));  // open: cin, cout
  ROM #(.addrWidth(16), .dataWidth(16)) rom_1 (.addr(register_1_q), .data({op_code, RS, RT, RD_Imm}));  // open: sel
  Register_File register_file_1 (
    .in_1(Result), .RD(RD_Imm), .RS(RS), .RT(RT), .Enable_Writing(in_6), .in_6(clock_1_out), .out_7(out_9),
    .out_8(out_15));
  _16_bit_ALU u_16_bit_alu_1 (
    .A(out_9), .ALU_op(in_4), .out_7(Result), .in_2(in_2), .Zero(zero), .overflow(over_flow), .in_1(in_1),
    .in_3(in_3), .B(out_15));

  // Notes on the sheet:
  //   writing data
  //   writhing enable
  //   clock
  //   PC
  //   contents of rom_1 (hex, n*v repeats v):
  //   123 330 5*0 101 0 0 0 1111 0 0 0 101
  //   Data 1
  //   Data 2
endmodule

module I__type_data_path (
  input  in_1,
  input  in_2,
  input  in_3,
  input  [1:0] in_4,
  input  in_5,
  output [3:0] op_code,
  output [3:0] RS,
  output [15:0] out_8,
  output [3:0] RT,
  output [3:0] RD_Imm,
  output zero,
  output [15:0] Result,
  output over_flow,
  output [15:0] out_14
);

  wire clock_1_out;
  wire [15:0] adder_1_out, register_1_q;

  Clock clock_1 (.out(clock_1_out));
  Register #(.width(16)) register_1 (.D(adder_1_out), .Q(register_1_q), .clk(clock_1_out));  // open: en, clr
  Adder #(.width(16)) adder_1 (.a(register_1_q), .b(16'h1), .out(adder_1_out));  // open: cin, cout
  ROM #(.addrWidth(16), .dataWidth(16)) rom_1 (.addr(register_1_q), .data({op_code, RS, RT, RD_Imm}));  // open: sel
  assign out_14 = {{12{1'b0}}, RD_Imm};  // Bit_Extender bit_extender_1
  Register_File register_file_1 (
    .in_1(Result), .RD(RT), .RS(RS), .RT(RT), .Enable_Writing(in_5), .in_6(clock_1_out), .out_7(out_8));  // open: out_8
  _16_bit_ALU u_16_bit_alu_1 (
    .A(out_8), .ALU_op(in_4), .out_7(Result), .in_2(in_2), .Zero(zero), .overflow(over_flow), .in_1(in_1),
    .in_3(in_3), .B(out_14));

  // Notes on the sheet:
  //   writhing enable
  //   clock
  //   PC
  //   contents of rom_1 (hex, n*v repeats v):
  //   123 220 220 4*0 101 0 0 0 1111 0 0 0 101
  //   Data 1
  //   Data 2
endmodule

module load_store_data_path (
  input  in_1,
  input  in_2,
  input  in_3,
  input  [1:0] in_4,
  input  store,
  input  load,
  input  in_7,
  output [3:0] op_code,
  output [3:0] RS,
  output [15:0] out_10,
  output [3:0] RT,
  output [3:0] RD_Imm,
  output [15:0] Result,
  output zero,
  output [15:0] Result_2,
  output over_flow,
  output [15:0] out_17
);

  wire clock_1_out, or_1_out;
  wire [15:0] adder_1_out, bit_extender_1_out, register_1_q;

  Clock clock_1 (.out(clock_1_out));
  Register #(.width(16)) register_1 (.D(adder_1_out), .Q(register_1_q), .clk(clock_1_out));  // open: en, clr
  Adder #(.width(16)) adder_1 (.a(register_1_q), .b(16'h1), .out(adder_1_out));  // open: cin, cout
  ROM #(.addrWidth(16), .dataWidth(16)) rom_1 (.addr(register_1_q), .data({op_code, RS, RT, RD_Imm}));  // open: sel
  assign bit_extender_1_out = {{12{1'b0}}, RD_Imm};  // Bit_Extender bit_extender_1
  Register_File register_file_1 (
    .in_1(Result_2), .RD(RT), .RS(RS), .RT(RT), .Enable_Writing(in_7), .in_6(clock_1_out), .out_7(out_10),
    .out_8(out_17));
  _16_bit_ALU u_16_bit_alu_1 (
    .A(out_10), .ALU_op(in_4), .out_7(Result), .in_2(in_2), .Zero(zero), .overflow(over_flow), .in_1(in_1),
    .in_3(in_3), .B(bit_extender_1_out));
  RAM #(.addrWidth(16), .dataWidth(16), .bus("separate")) ram_1 (
    .addr(Result), .din(out_17), .data(Result_2), .str(store), .sel(or_1_out), .clk(clock_1_out), .ld(load));  // open: clr
  or or_1 (or_1_out, load, store);

  // Notes on the sheet:
  //   writhing enable
  //   clock
  //   PC
  //   contents of rom_1 (hex, n*v repeats v):
  //   123 123 220 4*0 101 0 0 0 1111 0 0 0 101
  //   Data 1
  //   Data 2
endmodule

module Data_path_all_together (
  input  in_1,
  input  in_2,
  input  in_3,
  input  in_4,
  input  in_5,
  input  in_6,
  input  [1:0] in_7,
  input  store,
  input  load,
  input  in_10,
  input  in_11,
  output [11:0] out_12,
  output [3:0] op_code,
  output [3:0] RS,
  output [15:0] out_15,
  output [3:0] RT,
  output [3:0] RD_Imm,
  output [15:0] Result,
  output out_19,
  output [15:0] Result_2,
  output out_21,
  output [15:0] out_22
);

  wire clock_1_out, or_1_out;
  wire [3:0] multiplexer_2_out;
  wire [15:0] adder_1_out, adder_2_out, bit_extender_1_out, bit_extender_2_out, multiplexer_1_out,
       multiplexer_3_out, multiplexer_4_out, register_1_q;

  Clock clock_1 (.out(clock_1_out));
  Multiplexer #(.width(16), .enable("false")) multiplexer_1 (
    .in0(adder_1_out), .in1(adder_2_out), .out(multiplexer_1_out), .sel(in_1));
  Register #(.width(16)) register_1 (.D(multiplexer_1_out), .Q(register_1_q), .clk(clock_1_out));  // open: en, clr
  Adder #(.width(16)) adder_1 (.a(register_1_q), .b(16'h1), .out(adder_1_out));  // open: cin, cout
  ROM #(.addrWidth(16), .dataWidth(16)) rom_1 (.addr(register_1_q), .data({op_code, out_12}));  // open: sel
  Multiplexer #(.width(4), .enable("false")) multiplexer_2 (
    .in0(out_12[3:0]), .in1(out_12[7:4]), .out(multiplexer_2_out), .sel(in_6));
  assign bit_extender_1_out = {{12{1'b0}}, out_12[3:0]};  // Bit_Extender bit_extender_1
  Register_File register_file_1 (
    .in_1(multiplexer_4_out), .RD(multiplexer_2_out), .RS(out_12[11:8]), .RT(out_12[7:4]),
    .Enable_Writing(in_11), .in_6(clock_1_out), .out_7(out_15), .out_8(out_22));
  assign bit_extender_2_out = {{4{1'b0}}, out_12};  // Bit_Extender bit_extender_2
  Adder #(.width(16)) adder_2 (.a(bit_extender_2_out), .b(adder_1_out), .out(adder_2_out));  // open: cin, cout
  _16_bit_ALU u_16_bit_alu_1 (
    .A(out_15), .ALU_op(in_7), .out_7(Result), .in_2(in_3), .Zero(out_19), .overflow(out_21), .in_1(in_2),
    .in_3(in_4), .B(multiplexer_3_out));
  Multiplexer #(.width(16), .enable("false")) multiplexer_3 (
    .in0(out_22), .in1(bit_extender_1_out), .out(multiplexer_3_out), .sel(in_5));
  RAM #(.addrWidth(16), .dataWidth(16), .bus("separate")) ram_1 (
    .addr(Result), .din(out_22), .data(Result_2), .str(store), .sel(or_1_out), .clk(clock_1_out), .ld(load));  // open: clr
  or or_1 (or_1_out, load, store);
  Multiplexer #(.width(16), .enable("false")) multiplexer_4 (
    .in0(Result), .in1(Result_2), .out(multiplexer_4_out), .sel(in_10));

  assign RD_Imm = out_12[3:0];
  assign RS = out_12[11:8];
  assign RT = out_12[7:4];

  // Notes on the sheet:
  //   load means- load to reg file from memory
  //   writhing enable
  //   clock
  //   Max-3: 0-direct result, 1-lw/sw result
  //   Max-4: 0-normal, 1-jump
  //   PC
  //   Max-1: 0 for R-type rd spesific and I, lw/sw- rd shoted with rt
  //   Max-2:Direct data 2 for R-type or extend for I or Lw/sw
  //   Mux4
  //   contents of rom_1 (hex, n*v repeats v):
  //   1 153 25a3 aa0 0 0 0 101 0 0 0 1111 0 0 0 101
  //   Mux1
  //   Data 1
  //   Mux2
  //   Data 2
  //   ALU op
  //   zero
  //   over flow
  //   Mux3
endmodule

module last_control_unit (
  input  op0,
  input  op1,
  input  op2,
  input  op3,
  output r_vs_i,
  output write_env,
  output aluop1,
  output aluop0,
  output b_inv,
  output lw,
  output sw,
  output mem_env,
  output res_mem_alu,
  output beq,
  output jump
);

  wire nand_1_out, nand_2_out, nand_3_out, nand_4_out, nand_5_out, nand_6_out, nand_7_out, nand_8_out,
       nand_9_out, nand_10_out, nand_11_out, nand_12_out, nand_13_out, nand_14_out, nand_15_out, nand_16_out,
       nand_17_out, nand_18_out, nand_19_out, nand_20_out, nand_21_out, nand_22_out, nand_23_out,
       nand_24_out, nand_25_out, nand_26_out, nand_27_out, nand_28_out, nand_29_out, nand_30_out,
       nand_31_out, nand_32_out, nand_33_out, nand_34_out, nand_35_out, nand_36_out, nand_37_out, nand_38_out;

  nand nand_1 (nand_1_out, op0, op0);
  nand nand_2 (nand_2_out, op2, op2);
  nand nand_3 (nand_3_out, op3, op3);
  nand nand_4 (nand_4_out, op0, op0);
  nand nand_5 (nand_5_out, op0, op0);
  nand nand_6 (nand_6_out, op1, op1);
  nand nand_7 (nand_7_out, op2, op2);
  nand nand_8 (nand_8_out, op2, op2);
  nand nand_9 (nand_9_out, op0, op0);
  nand nand_10 (nand_10_out, op1, op1);
  nand nand_11 (nand_11_out, op2, op2);
  nand nand_12 (nand_12_out, op3, op3);
  nand nand_13 (nand_13_out, op0, op0);
  nand nand_14 (nand_14_out, op1, op1);
  nand nand_15 (nand_15_out, op3, op3);
  nand nand_16 (nand_16_out, op1, op1);
  nand nand_17 (nand_17_out, op0, op0);
  nand nand_18 (nand_18_out, op1, op1);
  nand nand_19 (nand_19_out, op0, op0);
  nand nand_20 (nand_20_out, op1, op1);
  nand nand_21 (nand_21_out, op0, op2);
  nand nand_22 (nand_22_out, op0, op2);
  nand nand_23 (nand_23_out, nand_1_out, op2);
  nand nand_24 (nand_24_out, op0, nand_2_out);
  nand nand_25 (nand_25_out, op0, nand_3_out);
  nand nand_26 (nand_26_out, nand_4_out, op3);
  nand nand_27 (nand_27_out, op1, op1);
  nand nand_28 (nand_28_out, nand_5_out, nand_6_out);
  nand nand_29 (nand_29_out, op2, op2);
  nand nand_30 (nand_30_out, op1, nand_7_out, op3);
  nand nand_31 (nand_31_out, op0, nand_8_out, op3);
  nand nand_32 (nand_32_out, nand_9_out, nand_10_out, nand_11_out, op3);
  nand nand_33 (nand_33_out, op1, op2, op3);
  nand nand_34 (nand_34_out, op0, op2, nand_12_out);
  nand nand_35 (nand_35_out, nand_13_out, nand_14_out, op2, nand_15_out);
  nand nand_36 (nand_36_out, nand_16_out, op2, op3);
  nand nand_37 (nand_37_out, nand_17_out, nand_18_out, op2);
  nand nand_38 (nand_38_out, nand_19_out, nand_20_out, op2);
  nand nand_39 (beq, nand_21_out, nand_21_out);
  nand nand_40 (jump, nand_22_out, nand_22_out);
  nand nand_41 (r_vs_i, nand_23_out, nand_24_out, nand_25_out);
  nand nand_42 (write_env, op2, nand_26_out, nand_27_out);
  nand nand_43 (aluop1, nand_28_out, nand_29_out);
  nand nand_44 (aluop0, nand_30_out, nand_31_out);
  nand nand_45 (b_inv, nand_32_out, nand_33_out, nand_34_out);
  nand nand_46 (lw, nand_35_out, nand_35_out);
  nand nand_47 (sw, nand_36_out, nand_36_out);
  nand nand_48 (mem_env, nand_37_out, nand_37_out);
  nand nand_49 (res_mem_alu, nand_38_out, nand_38_out);
endmodule

module full_data_path_with_control_unit (
  input  in_1,
  input  in_2,
  input  in_3,
  output [3:0] out_4,
  output [11:0] out_5,
  output [3:0] RS,
  output [15:0] out_7,
  output [3:0] RT,
  output [3:0] RD_Imm,
  output [15:0] Result,
  output out_11,
  output [15:0] Result_2,
  output out_13,
  output [15:0] out_14
);

  wire clock_1_out, last_control_unit_1_b_inv, last_control_unit_1_jump, last_control_unit_1_lw,
       last_control_unit_1_r_vs_i, last_control_unit_1_res_mem_alu, last_control_unit_1_sw,
       last_control_unit_1_write_env, or_1_out;
  wire [1:0] last_control_unit_1_aluop0;
  wire [3:0] multiplexer_2_out;
  wire [15:0] adder_1_out, adder_2_out, bit_extender_1_out, bit_extender_2_out, multiplexer_1_out,
       multiplexer_3_out, multiplexer_4_out, register_1_q;

  Clock clock_1 (.out(clock_1_out));
  Multiplexer #(.width(16), .enable("false")) multiplexer_1 (
    .in0(adder_1_out), .in1(adder_2_out), .out(multiplexer_1_out), .sel(last_control_unit_1_jump));
  Register #(.width(16)) register_1 (.D(multiplexer_1_out), .Q(register_1_q), .clk(clock_1_out));  // open: en, clr
  Adder #(.width(16)) adder_1 (.a(register_1_q), .b(16'h1), .out(adder_1_out));  // open: cin, cout
  ROM #(.addrWidth(16), .dataWidth(16)) rom_1 (.addr(register_1_q), .data({out_4, out_5}));  // open: sel
  Multiplexer #(.width(4), .enable("false")) multiplexer_2 (
    .in0(out_5[3:0]), .in1(out_5[7:4]), .out(multiplexer_2_out), .sel(last_control_unit_1_r_vs_i));
  assign bit_extender_1_out = {{12{1'b0}}, out_5[3:0]};  // Bit_Extender bit_extender_1
  Register_File register_file_1 (
    .in_1(multiplexer_4_out), .RD(multiplexer_2_out), .RS(out_5[11:8]), .RT(out_5[7:4]),
    .Enable_Writing(last_control_unit_1_write_env), .in_6(clock_1_out), .out_7(out_7), .out_8(out_14));
  last_control_unit last_control_unit_1 (
    .op0(out_4[3]), .op1(out_4[2]), .op2(out_4[1]), .op3(out_4[0]), .r_vs_i(last_control_unit_1_r_vs_i),
    .write_env(last_control_unit_1_write_env), .aluop1(last_control_unit_1_aluop0[1]),
    .aluop0(last_control_unit_1_aluop0[0]), .b_inv(last_control_unit_1_b_inv), .lw(last_control_unit_1_lw),
    .sw(last_control_unit_1_sw), .res_mem_alu(last_control_unit_1_res_mem_alu),
    .jump(last_control_unit_1_jump));  // open: mem_env, beq
  assign bit_extender_2_out = {{4{1'b0}}, out_5};  // Bit_Extender bit_extender_2
  Multiplexer #(.width(16), .enable("false")) multiplexer_3 (
    .in0(out_14), .in1(bit_extender_1_out), .out(multiplexer_3_out), .sel(in_3));
  Adder #(.width(16)) adder_2 (.a(bit_extender_2_out), .b(adder_1_out), .out(adder_2_out));  // open: cin, cout
  _16_bit_ALU u_16_bit_alu_1 (
    .A(out_7), .ALU_op(last_control_unit_1_aluop0), .out_7(Result), .in_2(in_2), .Zero(out_11),
    .overflow(out_13), .in_1(in_1), .in_3(last_control_unit_1_b_inv), .B(multiplexer_3_out));
  RAM #(.addrWidth(16), .dataWidth(16), .bus("separate")) ram_1 (
    .addr(Result), .din(out_14), .data(Result_2), .str(last_control_unit_1_sw), .sel(or_1_out),
    .clk(clock_1_out), .ld(last_control_unit_1_lw));  // open: clr
  or or_1 (or_1_out, last_control_unit_1_lw, last_control_unit_1_sw);
  Multiplexer #(.width(16), .enable("false")) multiplexer_4 (
    .in0(Result), .in1(Result_2), .out(multiplexer_4_out), .sel(last_control_unit_1_res_mem_alu));

  assign RD_Imm = out_5[3:0];
  assign RS = out_5[11:8];
  assign RT = out_5[7:4];

  // Notes on the sheet:
  //   clock
  //   Max-3: 0-direct result, 1-lw/sw result
  //   Max-4: 0-normal, 1-jump
  //   PC
  //   Max-1: 0 for R-type rd spesific and I, lw/sw- rd shoted with rt
  //   Max-2:Direct data 2 for R-type or extend for I or Lw/sw
  //   Mux4
  //   contents of rom_1 (hex, n*v repeats v):
  //   5000 2155 1123 aa0 0 0 0 101 0 0 0 1111 0 0 0 101
  //   op-code
  //   Mux1
  //   writhing enable
  //   Data 1
  //   Mux2
  //   Data 2
  //   ALU op
  //   zero
  //   over flow
  //   store
  //   load
  //   Mux3
endmodule

module beq (
  input  in_1,
  input  beq,
  input  in_3,
  input  in_4,
  input  in_5,
  input  in_6,
  input  in_7,
  input  [1:0] in_8,
  input  store,
  input  load,
  input  out,
  input  in_12,
  input  in_13,
  output [11:0] out_14,
  output [3:0] op_code,
  output [3:0] RS,
  output [15:0] out_17,
  output [3:0] RT,
  output [3:0] RD_Imm,
  output [15:0] Result,
  output out_21,
  output [15:0] Result_2,
  output out_23,
  output [15:0] out_24
);

  wire and_1_out, clock_1_out, or_1_out;
  wire [3:0] multiplexer_2_out;
  wire [15:0] adder_1_out, adder_2_out, adder_3_out, bit_extender_1_out, bit_extender_2_out,
       multiplexer_1_out, multiplexer_3_out, multiplexer_4_out, multiplexer_5_out, register_1_q;

  Clock clock_1 (.out(clock_1_out));
  Multiplexer #(.width(16), .enable("false")) multiplexer_1 (
    .in0(adder_1_out), .in1(adder_2_out), .out(multiplexer_1_out), .sel(in_1));
  Register #(.width(16)) register_1 (.D(multiplexer_4_out), .Q(register_1_q), .clk(clock_1_out));  // open: en, clr
  Adder #(.width(16)) adder_1 (.a(register_1_q), .b(16'h1), .out(adder_1_out));  // open: cin, cout
  ROM #(.addrWidth(16), .dataWidth(16)) rom_1 (.addr(register_1_q), .data({op_code, out_14}));  // open: sel
  Multiplexer #(.width(4), .enable("false")) multiplexer_2 (
    .in0(out_14[3:0]), .in1(out_14[7:4]), .out(multiplexer_2_out), .sel(in_7));
  assign bit_extender_1_out = {{12{1'b0}}, out_14[3:0]};  // Bit_Extender bit_extender_1
  Register_File register_file_1 (
    .in_1(multiplexer_5_out), .RD(multiplexer_2_out), .RS(out_14[11:8]), .RT(out_14[7:4]),
    .Enable_Writing(in_13), .in_6(clock_1_out), .out_7(out_17), .out_8(out_24));
  assign bit_extender_2_out = {{4{1'b0}}, out_14};  // Bit_Extender bit_extender_2
  Adder #(.width(16)) adder_2 (.a(bit_extender_2_out), .b(adder_1_out), .out(adder_2_out));  // open: cin, cout
  _16_bit_ALU u_16_bit_alu_1 (
    .A(out_17), .ALU_op(in_8), .out_7(Result), .in_2(in_4), .Zero(out_21), .overflow(out_23), .in_1(in_3),
    .in_3(in_5), .B(multiplexer_3_out));
  Multiplexer #(.width(16), .enable("false")) multiplexer_3 (
    .in0(out_24), .in1(bit_extender_1_out), .out(multiplexer_3_out), .sel(in_6));
  Adder #(.width(16)) adder_3 (.a(adder_1_out), .b(bit_extender_1_out), .out(adder_3_out));  // open: cin, cout
  Multiplexer #(.width(16), .enable("false")) multiplexer_4 (
    .in0(multiplexer_1_out), .in1(adder_3_out), .out(multiplexer_4_out), .sel(and_1_out));
  and and_1 (and_1_out, out_21, beq);
  RAM #(.addrWidth(16), .dataWidth(16), .bus("separate")) ram_1 (
    .addr(Result), .din(out_24), .data(Result_2), .str(store), .sel(or_1_out), .clk(clock_1_out), .ld(load));  // open: clr
  or or_1 (or_1_out, load, store);
  Multiplexer #(.width(16), .enable("false")) multiplexer_5 (
    .in0(Result), .in1(Result_2), .out(multiplexer_5_out), .sel(in_12));

  assign RD_Imm = out_14[3:0];
  assign RS = out_14[11:8];
  assign RT = out_14[7:4];

  // Notes on the sheet:
  //   load means- load to reg file from memory
  //   writhing enable
  //   clock
  //   Max-3: 0-direct result, 1-lw/sw result
  //   Max-4: 0-normal, 1-jump
  //   PC
  //   Max-1: 0 for R-type rd spesific and I, lw/sw- rd shoted with rt
  //   Max-2:Direct data 2 for R-type or extend for I or Lw/sw
  //   Mux4
  //   contents of rom_1 (hex, n*v repeats v):
  //   123 2155 25a3 aa0 563 0 0 101 13 123 123 1111 0 0 0 101
  //   Mux1
  //   Data 1
  //   Mux2
  //   Data 2
  //   ALU op
  //   zero
  //   over flow
  //   Mux 5
  //   If mux5 0- jump or 1 beq jump
  //   Mux3
endmodule

module control_unit (
  input  a,
  input  b,
  input  op1,
  input  c,
  output rd_rt,
  output w_env,
  output alu_op_2,
  output alu_op_1,
  output b_inv,
  output lw,
  output sw,
  output mem_env,
  output res_alu,
  output beq,
  output jump
);

  wire and_1_out, and_2_out, and_3_out, and_4_out, and_5_out, and_6_out, and_7_out, and_8_out, and_9_out,
       and_10_out, and_11_out, and_12_out, and_13_out, and_14_out, and_15_out, and_16_out, and_17_out,
       and_18_out, and_19_out, and_20_out, and_21_out, and_22_out, nand_1_out, nand_2_out, nand_3_out,
       nand_4_out, nand_5_out, nand_6_out, nand_7_out, nand_8_out, nand_9_out, nand_10_out, nand_11_out,
       nand_12_out, nand_13_out, nand_14_out, nand_15_out, nand_16_out, nand_17_out, nand_18_out,
       nand_19_out, nand_20_out, nand_21_out, nand_22_out, nand_23_out, nand_24_out, nand_25_out,
       nand_26_out, nand_27_out, nand_28_out, nand_29_out, nand_30_out, nand_31_out, nand_33_out,
       nand_34_out, nand_35_out, nand_36_out, nand_37_out, nand_38_out, nand_39_out, nand_40_out,
       nand_41_out, nand_42_out, nand_43_out, nand_44_out, nand_45_out, nand_49_out, nand_50_out;

  nand nand_1 (nand_1_out, a, a);
  nand nand_2 (nand_2_out, op1, op1);
  nand nand_3 (nand_3_out, c, c);
  nand nand_4 (nand_4_out, a, a);
  nand nand_5 (nand_5_out, a, a);
  nand nand_6 (nand_6_out, b, b);
  nand nand_7 (nand_7_out, op1, op1);
  nand nand_8 (nand_8_out, op1, op1);
  nand nand_9 (nand_9_out, a, a);
  nand nand_10 (nand_10_out, b, b);
  nand nand_11 (nand_11_out, op1, op1);
  nand nand_12 (nand_12_out, a, a);
  nand nand_13 (nand_13_out, b, b);
  nand nand_14 (nand_14_out, c, c);
  nand nand_15 (nand_15_out, a, a);
  nand nand_16 (nand_16_out, b, b);
  nand nand_17 (nand_17_out, a, a);
  nand nand_18 (nand_18_out, b, b);
  nand nand_19 (nand_19_out, a, a);
  nand nand_20 (nand_20_out, b, b);
  and and_1 (and_1_out, a, op1);
  nand nand_21 (nand_21_out, c, c);
  and and_2 (and_2_out, a, op1);
  and and_3 (and_3_out, a, b);
  nand nand_22 (nand_22_out, nand_1_out, op1);
  nand nand_23 (nand_23_out, a, nand_2_out);
  nand nand_24 (nand_24_out, a, nand_3_out);
  nand nand_25 (nand_25_out, a, b);
  nand nand_26 (nand_26_out, nand_4_out, c);
  nand nand_27 (nand_27_out, nand_5_out, nand_6_out);
  nand nand_28 (nand_28_out, op1, op1);
  and and_4 (and_4_out, b, nand_7_out);
  and and_5 (and_5_out, a, nand_8_out);
  and and_6 (and_6_out, nand_9_out, nand_10_out);
  and and_7 (and_7_out, nand_11_out, c);
  and and_8 (and_8_out, b, op1);
  and and_9 (and_9_out, nand_12_out, nand_13_out);
  and and_10 (and_10_out, op1, nand_14_out);
  and and_11 (and_11_out, nand_15_out, nand_16_out);
  and and_12 (and_12_out, op1, c);
  and and_13 (and_13_out, nand_17_out, nand_18_out);
  and and_14 (and_14_out, nand_19_out, nand_20_out);
  nand nand_29 (nand_29_out, and_1_out, nand_21_out);
  nand nand_30 (nand_30_out, a, b);
  and and_15 (and_15_out, and_2_out, c);
  or or_1 (jump, and_15_out, and_16_out);
  and and_16 (and_16_out, and_3_out, op1);
  and and_17 (and_17_out, nand_22_out, nand_23_out);
  and and_18 (and_18_out, nand_24_out, nand_25_out);
  and and_19 (and_19_out, op1, nand_26_out);
  nand nand_31 (nand_31_out, b, b);
  nand nand_32 (alu_op_2, nand_27_out, nand_28_out);
  nand nand_33 (nand_33_out, and_4_out, c);
  nand nand_34 (nand_34_out, and_5_out, c);
  nand nand_35 (nand_35_out, and_6_out, and_7_out);
  nand nand_36 (nand_36_out, and_8_out, c);
  and and_20 (and_20_out, a, op1);
  nand nand_37 (nand_37_out, c, c);
  nand nand_38 (nand_38_out, and_9_out, and_10_out);
  nand nand_39 (nand_39_out, a, b);
  nand nand_40 (nand_40_out, and_11_out, and_12_out);
  nand nand_41 (nand_41_out, a, b);
  nand nand_42 (nand_42_out, and_13_out, op1);
  nand nand_43 (nand_43_out, a, b);
  nand nand_44 (nand_44_out, and_14_out, op1);
  nand nand_45 (nand_45_out, a, b);
  nand nand_46 (beq, nand_29_out, nand_30_out);
  nand nand_47 (rd_rt, and_17_out, and_18_out);
  nand nand_48 (w_env, and_19_out, nand_31_out);
  and and_21 (and_21_out, nand_33_out, nand_34_out);
  nand nand_49 (nand_49_out, a, b);
  and and_22 (and_22_out, nand_35_out, nand_36_out);
  nand nand_50 (nand_50_out, and_20_out, nand_37_out);
  nand nand_51 (lw, nand_38_out, nand_39_out);
  nand nand_52 (sw, nand_40_out, nand_41_out);
  nand nand_53 (mem_env, nand_42_out, nand_43_out);
  nand nand_54 (res_alu, nand_44_out, nand_45_out);
  nand nand_55 (alu_op_1, and_21_out, nand_49_out);
  nand nand_56 (b_inv, and_22_out, nand_50_out);
endmodule

module sll (
  input  in_1,
  input  in_2,
  input  in_3,
  input  in_4,
  input  in_5,
  input  in_6,
  input  [1:0] in_7,
  input  store,
  input  load,
  input  in_10,
  input  [1:0] in_11,
  output [11:0] out_12,
  output [3:0] op_code,
  output [3:0] RS,
  output [15:0] out_15,
  output [3:0] RT,
  output [3:0] RD_Imm,
  output [15:0] Result,
  output out_19,
  output [15:0] Result_2,
  output out_21,
  output [15:0] out_22,
  output [15:0] out_23,
  output [15:0] after_shift,
  output [15:0] out_25
);

  wire clock_1_out, or_1_out;
  wire [3:0] bit_extender_3_out, multiplexer_2_out;
  wire [15:0] adder_1_out, adder_2_out, bit_extender_2_out, multiplexer_1_out, multiplexer_3_out,
       register_1_q;

  Clock clock_1 (.out(clock_1_out));
  Multiplexer #(.width(16), .enable("false")) multiplexer_1 (
    .in0(adder_1_out), .in1(adder_2_out), .out(multiplexer_1_out), .sel(in_1));
  Register #(.width(16)) register_1 (.D(multiplexer_1_out), .Q(register_1_q), .clk(clock_1_out));  // open: en, clr
  Adder #(.width(16)) adder_1 (.a(register_1_q), .b(16'h1), .out(adder_1_out));  // open: cin, cout
  ROM #(.addrWidth(16), .dataWidth(16)) rom_1 (.addr(register_1_q), .data({op_code, out_12}));  // open: sel
  Multiplexer #(.width(4), .enable("false")) multiplexer_2 (
    .in0(out_12[3:0]), .in1(out_12[7:4]), .out(multiplexer_2_out), .sel(in_6));
  assign out_25 = {{12{1'b0}}, out_12[3:0]};  // Bit_Extender bit_extender_1
  Register_File register_file_1 (
    .in_1(out_22), .RD(multiplexer_2_out), .RS(out_12[11:8]), .RT(out_12[7:4]), .Enable_Writing(in_10),
    .in_6(clock_1_out), .out_7(out_15), .out_8(out_23));
  assign bit_extender_2_out = {{4{1'b0}}, out_12};  // Bit_Extender bit_extender_2
  Adder #(.width(16)) adder_2 (.a(bit_extender_2_out), .b(adder_1_out), .out(adder_2_out));  // open: cin, cout
  _16_bit_ALU u_16_bit_alu_1 (
    .A(out_15), .ALU_op(in_7), .out_7(Result), .in_2(in_3), .Zero(out_19), .overflow(out_21), .in_1(in_2),
    .in_3(in_4), .B(multiplexer_3_out));
  Multiplexer #(.width(16), .enable("false")) multiplexer_3 (
    .in0(out_23), .in1(out_25), .out(multiplexer_3_out), .sel(in_5));
  Bit_Extender #(.in_width(16), .out_width(4)) bit_extender_3 (.in(out_25), .out(bit_extender_3_out));
  RAM #(.addrWidth(16), .dataWidth(16), .bus("separate")) ram_1 (
    .addr(Result), .din(out_23), .data(Result_2), .str(store), .sel(or_1_out), .clk(clock_1_out), .ld(load));  // open: clr
  or or_1 (or_1_out, load, store);
  Shifter #(.width(16)) shifter_1 (.in(out_15), .\dist (bit_extender_3_out), .out(after_shift));
  Multiplexer #(.select(2), .width(16), .enable("false")) multiplexer_4 (
    .in0(Result), .in1(Result_2), .in2(after_shift), .out(out_22), .sel(in_11));  // open: in3

  assign RD_Imm = out_12[3:0];
  assign RS = out_12[11:8];
  assign RT = out_12[7:4];

  // Notes on the sheet:
  //   load means- load to reg file from memory
  //   writhing enable
  //   clock
  //   Max-3: 0-direct result, 1-lw/sw result
  //   Max-4: 0-normal, 1-jump
  //   PC
  //   Max-1: 0 for R-type rd spesific and I, lw/sw- rd shoted with rt
  //   Max-2:Direct data 2 for R-type or extend for I or Lw/sw
  //   Mux4
  //   contents of rom_1 (hex, n*v repeats v):
  //   123 153 25a3 aa0 0 0 0 101 0 0 0 1111 0 0 0 101
  //   Mux 2
  //   Mux1
  //   immidate value
  //   Data 1
  //   Mux2
  //   Data 2
  //   ALU op
  //   data 1
  //   zero
  //   over flow
  //   shifter
  //   Mux3
  //   0-for normal result
  //   1 for load store
  //   10 for sll
endmodule

module immiadate_spliter_for_sing_bit (
  input  in_1,
  input  control_unit,
  input  in_3,
  input  in_4,
  input  in_5,
  input  in_6,
  input  [1:0] in_7,
  input  store,
  input  load,
  input  in_10,
  input  [1:0] in_11,
  output [11:0] out_12,
  output [3:0] op_code,
  output [3:0] RS,
  output [15:0] out_15,
  output [3:0] RT,
  output [3:0] RD_Imm,
  output [15:0] Result,
  output zero,
  output [15:0] Result_2,
  output over_flow,
  output [15:0] out_22,
  output [15:0] out_23,
  output [15:0] after_shift,
  output [15:0] out_25
);

  wire clock_1_out, or_1_out, or_2_out;
  wire [3:0] bit_extender_3_out, multiplexer_2_out;
  wire [15:0] adder_1_out, adder_2_out, bit_extender_2_out, multiplexer_1_out, multiplexer_3_out,
       register_1_q;

  Clock clock_1 (.out(clock_1_out));
  Multiplexer #(.width(16), .enable("false")) multiplexer_1 (
    .in0(adder_1_out), .in1(adder_2_out), .out(multiplexer_1_out), .sel(in_1));
  Register #(.width(16)) register_1 (.D(multiplexer_1_out), .Q(register_1_q), .clk(clock_1_out));  // open: en, clr
  Adder #(.width(16)) adder_1 (.a(register_1_q), .b(16'h1), .out(adder_1_out));  // open: cin, cout
  ROM #(.addrWidth(16), .dataWidth(16)) rom_1 (.addr(register_1_q), .data({op_code, out_12}));  // open: sel
  Multiplexer #(.width(4), .enable("false")) multiplexer_2 (
    .in0(out_12[3:0]), .in1(out_12[7:4]), .out(multiplexer_2_out), .sel(in_6));
  assign out_25 = {{13{1'b0}}, out_12[2:0]};  // Bit_Extender bit_extender_1
  Register_File register_file_1 (
    .in_1(out_22), .RD(multiplexer_2_out), .RS(out_12[11:8]), .RT(out_12[7:4]), .Enable_Writing(in_10),
    .in_6(clock_1_out), .out_7(out_15), .out_8(out_23));
  assign bit_extender_2_out = {{4{1'b0}}, out_12};  // Bit_Extender bit_extender_2
  Adder #(.width(16)) adder_2 (.a(bit_extender_2_out), .b(adder_1_out), .out(adder_2_out));  // open: cin, cout
  _16_bit_ALU u_16_bit_alu_1 (
    .A(out_15), .ALU_op(in_7), .out_7(Result), .in_2(in_4), .Zero(zero), .overflow(over_flow), .in_1(in_3),
    .in_3(or_1_out), .B(multiplexer_3_out));
  Multiplexer #(.width(16), .enable("false")) multiplexer_3 (
    .in0(out_23), .in1(out_25), .out(multiplexer_3_out), .sel(in_5));
  Bit_Extender #(.in_width(16), .out_width(4)) bit_extender_3 (.in(out_25), .out(bit_extender_3_out));
  or or_1 (or_1_out, control_unit, out_12[3]);
  RAM #(.addrWidth(16), .dataWidth(16), .bus("separate")) ram_1 (
    .addr(Result), .din(out_23), .data(Result_2), .str(store), .sel(or_2_out), .clk(clock_1_out), .ld(load));  // open: clr
  or or_2 (or_2_out, load, store);
  Shifter #(.width(16)) shifter_1 (.in(out_15), .\dist (bit_extender_3_out), .out(after_shift));
  Multiplexer #(.select(2), .width(16), .enable("false")) multiplexer_4 (
    .in0(Result), .in1(Result_2), .in2(after_shift), .out(out_22), .sel(in_11));  // open: in3

  assign RD_Imm = out_12[3:0];
  assign RS = out_12[11:8];
  assign RT = out_12[7:4];

  // Notes on the sheet:
  //   writhing enable
  //   clock
  //   Max-3: 0-direct result, 1-lw/sw result
  //   Max-4: 0-normal, 1-jump
  //   load means- load to reg file from memory
  //   PC
  //   Max-1: 0 for R-type rd spesific and I, lw/sw- rd shoted with rt
  //   Max-2:Direct data 2 for R-type or extend for I or Lw/sw
  //   Mux4
  //   contents of rom_1 (hex, n*v repeats v):
  //   123 153 25a3 aa0 0 0 0 101 0 0 0 1111 0 0 0 101
  //   Mux 2
  //   Mux1
  //   Data 1
  //   Mux2
  //   immidate value
  //   Data 2
  //   ALU op
  //   data 1
  //   shifter
  //   Mux3
  //   0-for normal result
  //   1 for load store
  //   10 for sll
endmodule
